# Fritzing sketch Reverse Geocache - Fritzing (saved by Fritzing 0.9.3b)

parts:
  ESP32_Development_Board = MH-ET LIVE ESP32 DEVKIT 38 pins
  Piezo_buzzer = Piezo Speaker
  NEO-6M_GPS_Receiver = NEO-6M GPS Module [part_number=GY-GPS6MV2]
  Electronic_lock_servo = Basic Servo
  S1 = Square Pushbutton
  128x32_OLED = Grove OLED 128x96
  Polulu_Pushbutton_Power_Switch_LV = Pololu Power Switch-LV
  USB_powerbank = Battery Holders [package=lipo-1100mAh]

nets:
  3V3: ESP32_Development_Board.3V3, 128x32_OLED.VCC
  N1: ESP32_Development_Board.GND#58, NEO-6M_GPS_Receiver.GND
  5V: ESP32_Development_Board.5V, Electronic_lock_servo.vcc
  GND: ESP32_Development_Board.GND#64, Piezo_buzzer.pin1, Electronic_lock_servo.gnd, 128x32_OLED.GND
  N2: ESP32_Development_Board.IO23, Electronic_lock_servo.pulse
  N3: ESP32_Development_Board.IO22, 128x32_OLED.SDA
  N4: ESP32_Development_Board.IO21, 128x32_OLED.SCL
  N5: ESP32_Development_Board.IO19, Piezo_buzzer.pin2
  N6: ESP32_Development_Board.IO17, NEO-6M_GPS_Receiver.Rx
  N7: ESP32_Development_Board.IO16, NEO-6M_GPS_Receiver.Tx
  N8: ESP32_Development_Board.IO4, Polulu_Pushbutton_Power_Switch_LV.A
  N9: S1.leg0, Polulu_Pushbutton_Power_Switch_LV.B
  N10: S1.leg1, Polulu_Pushbutton_Power_Switch_LV.ON
  N11: Polulu_Pushbutton_Power_Switch_LV.VIN, USB_powerbank.+
  N12: Polulu_Pushbutton_Power_Switch_LV.GND, USB_powerbank.-

notes:
  Power control pin

custom parts:
  MH-ET LIVE ESP32 DEVKIT 38 pins: http://mh.nodebb.com/topic/2/mh-et-live-esp32-devkit
  NEO-6M GPS Module: GY-GPS6MV2 NEO-6M GPS Module Module based on U-blox NEO-6M GPS engine, incorporating regulator for 3.3-5V DC input, MS621FE-compatible rechargeable battery for backup and EEPROM for storing configuration settings. Links: NEO-6 series product information page NEO-6 Datasheet
  Pololu Power Switch-LV: Mini Pushbutton Power Switch with Reverse Voltage Protection, LV
